// Logisim project Multiplicador-4bits.circ as structural Verilog: 1 circuit, main circuit Multiplicador-4bits
module Multiplicador_4bits (
  input  A3,
  input  A2,
  input  A1,
  input  A0,
  input  B3,
  input  B2,
  input  B1,
  input  B0,
  output S0,
  output S1,
  output S2,
  output S3,
  output S4,
  output S5,
  output S6,
  output S7
);

  wire adder_1_cout, adder_2_cout, adder_2_out, adder_3_cout, adder_3_out, adder_4_cout, adder_4_out,
       adder_5_cout, adder_5_out, adder_7_cout, adder_8_cout, adder_8_out, adder_9_cout, adder_9_out,
       adder_10_cout, adder_11_cout, adder_12_cout, and_2_out, and_3_out, and_4_out, and_5_out, and_6_out,
       and_7_out, and_8_out, and_9_out, and_10_out, and_11_out, and_12_out, and_13_out, and_14_out,
       and_15_out, and_16_out;

  and and_1 (S0, A0, B0);
  and and_2 (and_2_out, B0, A1);
  and and_3 (and_3_out, B1, A0);
  and and_4 (and_4_out, B0, A2);
  and and_5 (and_5_out, B1, A1);
  and and_6 (and_6_out, B2, A0);
  and and_7 (and_7_out, B0, A3);
  and and_8 (and_8_out, B1, A2);
  and and_9 (and_9_out, B2, A1);
  and and_10 (and_10_out, B3, A0);
  and and_11 (and_11_out, B1, A3);
  and and_12 (and_12_out, B2, A2);
  and and_13 (and_13_out, B3, A1);
  and and_14 (and_14_out, B2, A3);
  and and_15 (and_15_out, B3, A2);
  and and_16 (and_16_out, B3, A3);
  Adder #(.width(1)) adder_1 (.a(and_2_out), .b(and_3_out), .out(S1), .cin(1'b0), .cout(adder_1_cout));
  Adder #(.width(1)) adder_2 (.a(and_4_out), .b(and_5_out), .out(adder_2_out), .cin(adder_1_cout), .cout(adder_2_cout));
  Adder #(.width(1)) adder_3 (.a(and_7_out), .b(and_8_out), .out(adder_3_out), .cin(adder_2_cout), .cout(adder_3_cout));
  Adder #(.width(1)) adder_4 (.a(adder_3_cout), .b(and_11_out), .out(adder_4_out), .cin(1'b0), .cout(adder_4_cout));
  Adder #(.width(1)) adder_5 (
    .a(adder_4_cout), .b(and_14_out), .out(adder_5_out), .cin(adder_9_cout), .cout(adder_5_cout));
  Adder #(.width(1)) adder_6 (.a(adder_5_cout), .b(and_16_out), .out(S6), .cin(adder_12_cout), .cout(S7));
  Adder #(.width(1)) adder_7 (.a(adder_2_out), .b(and_6_out), .out(S2), .cin(1'b0), .cout(adder_7_cout));
  Adder #(.width(1)) adder_8 (
    .a(adder_3_out), .b(and_9_out), .out(adder_8_out), .cin(adder_7_cout), .cout(adder_8_cout));
  Adder #(.width(1)) adder_9 (
    .a(adder_4_out), .b(and_12_out), .out(adder_9_out), .cin(adder_8_cout), .cout(adder_9_cout));
  Adder #(.width(1)) adder_10 (.a(adder_8_out), .b(and_10_out), .out(S3), .cin(1'b0), .cout(adder_10_cout));
  Adder #(.width(1)) adder_11 (.a(adder_9_out), .b(and_13_out), .out(S4), .cin(adder_10_cout), .cout(adder_11_cout));
  Adder #(.width(1)) adder_12 (.a(adder_5_out), .b(and_15_out), .out(S5), .cin(adder_11_cout), .cout(adder_12_cout));
endmodule
